# Fritzing sketch VendoAirPump (saved by Fritzing 0.9.5d)

parts:
  A1 = 2957N11 pressure sensor
  M1 = 1 chan 5v relay module
  J2 = Camdenboss CTB0158-2 [part_number=CTB0158-2 package=THT]
  J1 = Camdenboss CTB0158-2 [part_number=CTB0158-2 package=THT]
  Part1 = Arduino Nano (Rev3.0)
  Raspberry_Pi_1 = Raspberry Pi 4 [part_number=RPI-4-b]  # not connected

nets:
  N1: A1.Pin_1, M1.pin_2, J1.pin1, Part1.GND
  N2: A1.Pin_2, M1.pin_1, Part1.5V
  N3: A1.Pin_3, Part1.A0
  N4: M1.pin_3, Part1.D3
  N5: M1.pin_5, J2.pin2
  N6: M1.pin_6, J2.pin1
  N7: J1.pin2, Part1.D2

custom parts:
  2957N11 pressure sensor: Monitor and control vacuum pumps, air compressors, and hydraulics. These transmitters convert both pressure and vacuum into an electrical signal that can be interpreted by receiving devices, such as remote displays, programmable logic controllers, and motor speed controls.
  1 chan 5v relay module: 1 Channel 5V Relay Module Board Shield with Optocoupler Support High and Low Level Trigger for Arduino.
  Raspberry Pi 4: The RPi4, a faster version of the awesome Raspberry Pi 2 B ARM Board with 40 pin gpio. Ready for special Raspberry Pi B+ and RPi2 Hat (Hardware attached (on) top)
